// Logisim project logic_circuits.circ as structural Verilog
// NOT
module e1_NOT (
  input  in_1,
  output out_2
);

  not not_1 (out_2, in_1);
endmodule

// AND
module e2_AND (
  input  A,
  input  B,
  output out_3
);

  and and_1 (out_3, A, B);
endmodule

// OR
module e3_OR (
  input  A,
  input  B,
  output out_3
);

  or or_1 (out_3, A, B);
endmodule

// NAND
module e4_NAND (
  input  A,
  input  B,
  output Output
);

  wire not_1_out, not_2_out;

  not not_1 (not_1_out, A);
  not not_2 (not_2_out, B);
  or or_1 (Output, not_1_out, not_2_out);
endmodule

// NOR
module e5_NOR (
  input  A,
  input  B,
  output out_3
);

  wire or_1_out;

  or or_1 (or_1_out, A, B);
  not not_1 (out_3, or_1_out);
endmodule

// XOR
module e6_XOR (
  input  A,
  input  B,
  output out_3
);

  wire and_1_out, and_2_out, not_1_out, not_2_out;

  not not_1 (not_1_out, B);
  not not_2 (not_2_out, A);
  and and_1 (and_1_out, A, not_1_out);
  and and_2 (and_2_out, not_2_out, B);
  or or_1 (out_3, and_1_out, and_2_out);
endmodule

// XNOR
module e7_XNOR (
  input  A,
  input  B,
  output out_3
);

  wire and_1_out, and_2_out, not_1_out, not_2_out, or_1_out;

  not not_1 (not_1_out, B);
  not not_2 (not_2_out, A);
  and and_1 (and_1_out, A, not_1_out);
  and and_2 (and_2_out, not_2_out, B);
  or or_1 (or_1_out, and_1_out, and_2_out);
  not not_3 (out_3, or_1_out);
endmodule

// LED
module e8_LED (
);

  wire button_1_out;

  Button button_1 (.out(button_1_out));
  LED led_1 (.in(button_1_out));
endmodule

// LEDs
module e9_LEDs (
);

  wire button_1_out, not_1_out;

  Button button_1 (.out(button_1_out));
  not not_1 (not_1_out, button_1_out);
  LED led_1 (.in(not_1_out));
  LED led_2 (.in(button_1_out));
endmodule

// 4AND
module e10_4AND (
  input  A,
  input  B,
  input  C,
  input  D,
  output Output
);

  wire e4_nand_1_output, e4_nand_2_output, e4_nand_3_output, e4_nand_4_output, e4_nand_5_output;

  e4_NAND e4_nand_1 (.A(A), .B(B), .Output(e4_nand_1_output));
  e4_NAND e4_nand_2 (.A(C), .B(D), .Output(e4_nand_2_output));
  e4_NAND e4_nand_3 (.A(e4_nand_1_output), .B(e4_nand_1_output), .Output(e4_nand_3_output));
  e4_NAND e4_nand_4 (.A(e4_nand_3_output), .B(e4_nand_5_output), .Output(e4_nand_4_output));
  e4_NAND e4_nand_5 (.A(e4_nand_2_output), .B(e4_nand_2_output), .Output(e4_nand_5_output));
  e4_NAND e4_nand_6 (.A(e4_nand_4_output), .B(e4_nand_4_output), .Output(Output));
endmodule

// 5OR
module e11_5OR (
  input  A,
  input  B,
  input  C,
  input  D,
  input  E,
  output out_6
);

  wire e5_nor_1_out_3, e5_nor_2_out_3, e5_nor_3_out_3, e5_nor_4_out_3, e5_nor_5_out_3, e5_nor_6_out_3,
       e5_nor_7_out_3;

  e5_NOR e5_nor_1 (.A(A), .B(B), .out_3(e5_nor_1_out_3));
  e5_NOR e5_nor_2 (.A(C), .B(D), .out_3(e5_nor_2_out_3));
  e5_NOR e5_nor_3 (.A(e5_nor_1_out_3), .B(e5_nor_1_out_3), .out_3(e5_nor_3_out_3));
  e5_NOR e5_nor_4 (.A(e5_nor_2_out_3), .B(e5_nor_2_out_3), .out_3(e5_nor_4_out_3));
  e5_NOR e5_nor_5 (.A(e5_nor_3_out_3), .B(e5_nor_4_out_3), .out_3(e5_nor_5_out_3));
  e5_NOR e5_nor_6 (.A(e5_nor_5_out_3), .B(e5_nor_5_out_3), .out_3(e5_nor_6_out_3));
  e5_NOR e5_nor_7 (.A(e5_nor_6_out_3), .B(E), .out_3(e5_nor_7_out_3));
  e5_NOR e5_nor_8 (.A(e5_nor_7_out_3), .B(e5_nor_7_out_3), .out_3(out_6));
endmodule

// 4XOR
module e12_4XOR (
  input  A,
  input  B,
  input  C,
  input  D,
  output Output
);

  wire e7_xnor_1_out_3, e7_xnor_2_out_3, e7_xnor_3_out_3, e7_xnor_4_out_3, e7_xnor_5_out_3;

  e7_XNOR e7_xnor_1 (.A(A), .B(B), .out_3(e7_xnor_1_out_3));
  e7_XNOR e7_xnor_2 (.A(e7_xnor_1_out_3), .B(1'b0), .out_3(e7_xnor_2_out_3));
  e7_XNOR e7_xnor_3 (.A(e7_xnor_2_out_3), .B(C), .out_3(e7_xnor_3_out_3));
  e7_XNOR e7_xnor_4 (.A(e7_xnor_3_out_3), .B(1'b0), .out_3(e7_xnor_4_out_3));
  e7_XNOR e7_xnor_5 (.A(e7_xnor_4_out_3), .B(D), .out_3(e7_xnor_5_out_3));
  e7_XNOR e7_xnor_6 (.A(e7_xnor_5_out_3), .B(1'b0), .out_3(Output));
endmodule

// SR_FF
module m1_SR_FF (
  input  Set,
  input  Reset,
  output Qn,
  output Qn_1
);

  wire clock_1_out, e4_nand_1_output, e4_nand_2_output;

  Clock clock_1 (.out(clock_1_out));
  e4_NAND e4_nand_1 (.A(Set), .B(clock_1_out), .Output(e4_nand_1_output));
  e4_NAND e4_nand_2 (.A(clock_1_out), .B(Reset), .Output(e4_nand_2_output));
  e4_NAND e4_nand_3 (.A(e4_nand_1_output), .B(Qn_1), .Output(Qn));
  e4_NAND e4_nand_4 (.A(Qn), .B(e4_nand_2_output), .Output(Qn_1));
endmodule

module m2_D_FF (
  input  D,
  output Qn,
  output Qn_1
);

  wire clock_1_out, e4_nand_1_output, e4_nand_2_output, e4_nand_3_output;

  Clock clock_1 (.out(clock_1_out));
  e4_NAND e4_nand_1 (.A(D), .B(D), .Output(e4_nand_1_output));
  e4_NAND e4_nand_2 (.A(D), .B(clock_1_out), .Output(e4_nand_2_output));
  e4_NAND e4_nand_3 (.A(clock_1_out), .B(e4_nand_1_output), .Output(e4_nand_3_output));
  e4_NAND e4_nand_4 (.A(e4_nand_2_output), .B(Qn_1), .Output(Qn));
  e4_NAND e4_nand_5 (.A(Qn), .B(e4_nand_3_output), .Output(Qn_1));
endmodule

// JK_FF
module m3_JK_MS_FF (
  input  Set,
  input  Reset,
  output Qn,
  output Qn_1
);

  wire and_1_out, and_2_out, and_3_out, and_4_out, clock_1_out, nor_1_out, nor_2_out, not_1_out, Start_out;

  Clock clock_1 (.out(clock_1_out));
  and and_1 (and_1_out, Qn_1, Set, clock_1_out);
  and and_2 (and_2_out, clock_1_out, Reset, Qn);
  not not_1 (not_1_out, clock_1_out);
  Button Start (.out(Start_out));
  nor nor_1 (nor_1_out, and_1_out, nor_2_out);
  nor nor_2 (nor_2_out, nor_1_out, and_2_out, Start_out);
  and and_3 (and_3_out, not_1_out, nor_1_out);
  and and_4 (and_4_out, nor_2_out, not_1_out);
  nor nor_3 (Qn, and_3_out, Qn_1);
  nor nor_4 (Qn_1, Qn, and_4_out);

  // Notes on the sheet:
  //   Hoever, using a master-slave JK flip flop overcomes this simulation problem.
  //   The point of having a JK Flip Flop is to overcome the racing condition problem in a SR Flip Flop i.e. when both inputs are 1. 
  //   While the JK Flip Flop can be constructed in Logisim as above, setting J and K simultaneously to 1 raises the oscillation error. 
  //   This defeats the purpose of having a JKFF as its resulting functionality would remain as a SR Flip Flop, not as actually intended; it functions NOT as how it actually does outside of simulation.
endmodule

module m4_T_FF (
  input  T,
  output Qn,
  output Qn_1
);

  wire and_1_out, and_2_out, and_3_out, and_4_out, clock_1_out, nor_1_out, nor_2_out, not_1_out, Start_out;

  Clock clock_1 (.out(clock_1_out));
  and and_1 (and_1_out, Qn_1, T, clock_1_out);
  and and_2 (and_2_out, clock_1_out, T, Qn);
  not not_1 (not_1_out, clock_1_out);
  Button Start (.out(Start_out));
  nor nor_1 (nor_1_out, and_1_out, nor_2_out);
  nor nor_2 (nor_2_out, nor_1_out, and_2_out, Start_out);
  and and_3 (and_3_out, not_1_out, nor_1_out);
  and and_4 (and_4_out, nor_2_out, not_1_out);
  nor nor_3 (Qn, and_3_out, Qn_1);
  nor nor_4 (Qn_1, Qn, and_4_out);

  // Notes on the sheet:
  //   Same as JK Flip Flop, but with connected external input
endmodule

module m5_REG (
  input  I1,
  input  I2,
  input  I3,
  input  I4,
  output D1,
  output D2,
  output D3,
  output D4
);

  wire and_1_out, clock_1_out, Load_out, Reset_out;

  Clock clock_1 (.out(clock_1_out));
  Button Load (.out(Load_out));
  and and_1 (and_1_out, clock_1_out, Load_out);
  D_Flip_Flop d_ff_1 (.clk(and_1_out), .D(I1), .Q(D1), .reset(Reset_out));  // open: Qn, preset, en
  D_Flip_Flop d_ff_2 (.clk(and_1_out), .D(I2), .Q(D2), .reset(Reset_out));  // open: Qn, preset, en
  D_Flip_Flop d_ff_3 (.clk(and_1_out), .D(I3), .Q(D3), .reset(Reset_out));  // open: Qn, preset, en
  D_Flip_Flop d_ff_4 (.clk(and_1_out), .D(I4), .Q(D4), .reset(Reset_out));  // open: Qn, preset, en
  Button Reset (.out(Reset_out));
endmodule

module m6_BIN_CNTR (
  output [3:0] out_1
);

  wire and_1_out, and_2_out, CLK_out;

  Clock CLK (.out(CLK_out));
  J_K_Flip_Flop j_k_ff_1 (.J(1'b1), .clk(CLK_out), .K(1'b1), .Q(out_1[0]));  // open: Qn, preset, en, reset
  J_K_Flip_Flop j_k_ff_2 (.J(out_1[0]), .clk(CLK_out), .K(out_1[0]), .Q(out_1[1]));  // open: Qn, preset, en, reset
  and and_1 (and_1_out, out_1[0], out_1[1]);
  J_K_Flip_Flop j_k_ff_3 (.J(and_1_out), .clk(CLK_out), .K(and_1_out), .Q(out_1[2]));  // open: Qn, preset, en, reset
  and and_2 (and_2_out, and_1_out, out_1[2]);
  J_K_Flip_Flop j_k_ff_4 (.J(and_2_out), .clk(CLK_out), .K(and_2_out), .Q(out_1[3]));  // open: Qn, preset, en, reset
endmodule

// 2MUX
module m9_2MUX (
  input  I0,
  input  I1,
  input  Switch,
  output Output
);

  wire e4_nand_1_output, e4_nand_2_output, not_1_out;

  not not_1 (not_1_out, Switch);
  e4_NAND e4_nand_1 (.A(I0), .B(Switch), .Output(e4_nand_1_output));
  e4_NAND e4_nand_2 (.A(I1), .B(not_1_out), .Output(e4_nand_2_output));
  e4_NAND e4_nand_3 (.A(e4_nand_1_output), .B(e4_nand_2_output), .Output(Output));
endmodule

module m10_4MUX (
  input  I0,
  input  I1,
  input  I2,
  input  I3,
  input  SW1,
  input  SW2,
  output Output
);

  wire and_1_out, and_2_out, and_3_out, and_4_out, not_1_out, not_2_out;

  not not_1 (not_1_out, SW1);
  not not_2 (not_2_out, SW2);
  and and_1 (and_1_out, not_1_out, not_2_out, I0);
  and and_2 (and_2_out, not_1_out, SW2, I1);
  and and_3 (and_3_out, SW1, not_2_out, I2);
  and and_4 (and_4_out, SW1, SW2, I3);
  or or_1 (Output, and_1_out, and_2_out, and_3_out, and_4_out);
endmodule

module m11_2DEMUX (
  input  F,
  input  SW,
  output A,
  output B
);

  wire not_1_out;

  not not_1 (not_1_out, SW);
  and and_1 (A, F, SW);
  and and_2 (B, F, not_1_out);
endmodule

module m12_4DEMUX (
  input  F,
  input  SW1,
  input  SW2,
  output A,
  output B,
  output C,
  output D
);

  wire not_1_out, not_2_out;

  not not_1 (not_1_out, SW1);
  not not_2 (not_2_out, SW2);
  and and_1 (A, not_1_out, not_2_out, F);
  and and_2 (B, not_1_out, SW2, F);
  and and_3 (C, SW1, not_2_out, F);
  and and_4 (D, SW1, SW2, F);
endmodule

module h1_CLK_REG (
  input  I1,
  input  I2,
  input  I3,
  input  I4,
  output D1,
  output D2,
  output D3,
  output D4
);

  wire Clock_out, Reset_out;

  Clock #(.lowDuration(3)) Clock (.out(Clock_out));
  D_Flip_Flop d_ff_1 (.clk(Clock_out), .D(I1), .Q(D1), .reset(Reset_out));  // open: Qn, preset, en
  D_Flip_Flop d_ff_2 (.clk(Clock_out), .D(I2), .Q(D2), .reset(Reset_out));  // open: Qn, preset, en
  D_Flip_Flop d_ff_3 (.clk(Clock_out), .D(I3), .Q(D3), .reset(Reset_out));  // open: Qn, preset, en
  D_Flip_Flop d_ff_4 (.clk(Clock_out), .D(I4), .Q(D4), .reset(Reset_out));  // open: Qn, preset, en
  Button Reset (.out(Reset_out));
endmodule

module h3_DELAY (
  input  Main_Signal,
  output Output_Signal
);

  wire clock_1_out, d_ff_1_q, h5_4cmprtr_1_a_b_2, s_r_ff_1_q, xor_1_out;
  wire [3:0] counter_1_q;

  Clock clock_1 (.out(clock_1_out));
  D_Flip_Flop d_ff_1 (.clk(clock_1_out), .D(Main_Signal), .Q(d_ff_1_q));  // open: Qn, preset, en, reset
  xor xor_1 (xor_1_out, Main_Signal, d_ff_1_q);
  S_R_Flip_Flop s_r_ff_1 (
    .S(xor_1_out), .clk(clock_1_out), .R(h5_4cmprtr_1_a_b_2), .Q(s_r_ff_1_q));  // open: Qn, preset, reset, en
  Counter #(.width(4), .max('ha)) counter_1 (
    .Q(counter_1_q), .clk(clock_1_out), .clr(xor_1_out));  // open: load, D, count, carry
  h5_4CMPRTR h5_4cmprtr_1 (.B(4'b1010), .A(counter_1_q), .A_B_2(h5_4cmprtr_1_a_b_2));  // open: A_B, A_B_3
  m9_2MUX m9_2mux_1 (.I0(s_r_ff_1_q), .I1(1'b0), .Switch(h5_4cmprtr_1_a_b_2), .Output(Output_Signal));
endmodule

// CMPRTR
module h5_4CMPRTR (
  input  [3:0] B,
  input  [3:0] A,
  output A_B,
  output A_B_2,
  output A_B_3
);

  wire and_1_out, and_2_out, and_3_out, and_4_out, e7_xnor_1_out_3, e7_xnor_2_out_3, e7_xnor_3_out_3,
       e7_xnor_4_out_3, not_1_out, not_2_out, not_3_out, not_4_out;

  not not_1 (not_1_out, B[3]);
  e7_XNOR e7_xnor_1 (.A(B[3]), .B(A[3]), .out_3(e7_xnor_1_out_3));
  not not_2 (not_2_out, B[2]);
  e7_XNOR e7_xnor_2 (.A(B[2]), .B(A[2]), .out_3(e7_xnor_2_out_3));
  not not_3 (not_3_out, B[1]);
  e7_XNOR e7_xnor_3 (.A(B[1]), .B(A[1]), .out_3(e7_xnor_3_out_3));
  not not_4 (not_4_out, B[0]);
  e7_XNOR e7_xnor_4 (.A(B[0]), .B(A[0]), .out_3(e7_xnor_4_out_3));
  and and_1 (and_1_out, not_1_out, A[3]);
  and and_2 (and_2_out, e7_xnor_1_out_3, not_2_out, A[2]);
  and and_3 (and_3_out, e7_xnor_2_out_3, e7_xnor_1_out_3, not_3_out, A[1]);
  and and_4 (and_4_out, e7_xnor_3_out_3, e7_xnor_2_out_3, e7_xnor_1_out_3, not_4_out, A[0]);
  or or_1 (A_B, and_1_out, and_2_out, and_3_out, and_4_out);
  and and_5 (A_B_2, e7_xnor_1_out_3, e7_xnor_2_out_3, e7_xnor_3_out_3, e7_xnor_4_out_3);
  e5_NOR e5_nor_1 (.A(A_B), .B(A_B_2), .out_3(A_B_3));
endmodule

module h8_8_FULL_ADDER (
  input  [7:0] A,
  input  [7:0] B,
  output Carry_Out,
  output [7:0] Sum
);

  wire custom_full_adder_1_carry_out, custom_full_adder_2_carry_out, custom_full_adder_3_carry_out,
       custom_full_adder_4_carry_out, custom_full_adder_5_carry_out, custom_full_adder_6_carry_out,
       custom_full_adder_8_carry_out;

  custom_FULL_ADDER custom_full_adder_1 (
    .A(A[1]), .B(B[1]), .Carry_IN(custom_full_adder_2_carry_out), .Carry_Out(custom_full_adder_1_carry_out),
    .Sum(Sum[1]));
  custom_FULL_ADDER custom_full_adder_2 (
    .A(A[0]), .B(B[0]), .Carry_IN(1'b0), .Carry_Out(custom_full_adder_2_carry_out), .Sum(Sum[0]));
  custom_FULL_ADDER custom_full_adder_3 (
    .A(A[2]), .B(B[2]), .Carry_IN(custom_full_adder_1_carry_out), .Carry_Out(custom_full_adder_3_carry_out),
    .Sum(Sum[2]));
  custom_FULL_ADDER custom_full_adder_4 (
    .A(A[4]), .B(B[4]), .Carry_IN(custom_full_adder_5_carry_out), .Carry_Out(custom_full_adder_4_carry_out),
    .Sum(Sum[4]));
  custom_FULL_ADDER custom_full_adder_5 (
    .A(A[3]), .B(B[3]), .Carry_IN(custom_full_adder_3_carry_out), .Carry_Out(custom_full_adder_5_carry_out),
    .Sum(Sum[3]));
  custom_FULL_ADDER custom_full_adder_6 (
    .A(A[5]), .B(B[5]), .Carry_IN(custom_full_adder_4_carry_out), .Carry_Out(custom_full_adder_6_carry_out),
    .Sum(Sum[5]));
  custom_FULL_ADDER custom_full_adder_7 (
    .A(A[7]), .B(B[7]), .Carry_IN(custom_full_adder_8_carry_out), .Carry_Out(Carry_Out), .Sum(Sum[7]));
  custom_FULL_ADDER custom_full_adder_8 (
    .A(A[6]), .B(B[6]), .Carry_IN(custom_full_adder_6_carry_out), .Carry_Out(custom_full_adder_8_carry_out),
    .Sum(Sum[6]));
endmodule

// BTWS_NOT
module h16_BTWS_NOT (
  input  [7:0] IN,
  output [7:0] OUT
);

  not not_1 (OUT[7], IN[7]);
  not not_2 (OUT[6], IN[6]);
  not not_3 (OUT[4], IN[4]);
  not not_4 (OUT[5], IN[5]);
  not not_5 (OUT[3], IN[3]);
  not not_6 (OUT[2], IN[2]);
  not not_7 (OUT[1], IN[1]);
  not not_8 (OUT[0], IN[0]);
endmodule

module h18_BIN_DEC (
  input  [7:0] in_1,
  output [3:0] Units,
  output [3:0] Tens,
  output [3:0] Hundreds
);

  wire custom_comparative_adder_1_o0, custom_comparative_adder_1_o1, custom_comparative_adder_1_o2,
       custom_comparative_adder_1_o3, custom_comparative_adder_2_o0, custom_comparative_adder_2_o1,
       custom_comparative_adder_2_o2, custom_comparative_adder_2_o3, custom_comparative_adder_3_o0,
       custom_comparative_adder_3_o1, custom_comparative_adder_3_o2, custom_comparative_adder_3_o3,
       custom_comparative_adder_4_o0, custom_comparative_adder_4_o1, custom_comparative_adder_4_o2,
       custom_comparative_adder_4_o3, custom_comparative_adder_5_o0, custom_comparative_adder_5_o1,
       custom_comparative_adder_5_o2;

  custom_COMPARATIVE_ADDER custom_comparative_adder_1 (
    .I0(in_1[5]), .I1(in_1[6]), .I2(in_1[7]), .I3(1'b0), .O0(custom_comparative_adder_1_o0),
    .O1(custom_comparative_adder_1_o1), .O2(custom_comparative_adder_1_o2), .O3(custom_comparative_adder_1_o3));
  custom_COMPARATIVE_ADDER custom_comparative_adder_2 (
    .I0(in_1[4]), .I1(custom_comparative_adder_1_o0), .I2(custom_comparative_adder_1_o1),
    .I3(custom_comparative_adder_1_o2), .O0(custom_comparative_adder_2_o0),
    .O1(custom_comparative_adder_2_o1), .O2(custom_comparative_adder_2_o2), .O3(custom_comparative_adder_2_o3));
  custom_COMPARATIVE_ADDER custom_comparative_adder_3 (
    .I0(in_1[3]), .I1(custom_comparative_adder_2_o0), .I2(custom_comparative_adder_2_o1),
    .I3(custom_comparative_adder_2_o2), .O0(custom_comparative_adder_3_o0),
    .O1(custom_comparative_adder_3_o1), .O2(custom_comparative_adder_3_o2), .O3(custom_comparative_adder_3_o3));
  custom_COMPARATIVE_ADDER custom_comparative_adder_4 (
    .I0(in_1[2]), .I1(custom_comparative_adder_3_o0), .I2(custom_comparative_adder_3_o1),
    .I3(custom_comparative_adder_3_o2), .O0(custom_comparative_adder_4_o0),
    .O1(custom_comparative_adder_4_o1), .O2(custom_comparative_adder_4_o2), .O3(custom_comparative_adder_4_o3));
  custom_COMPARATIVE_ADDER custom_comparative_adder_5 (
    .I0(custom_comparative_adder_3_o3), .I1(custom_comparative_adder_2_o3),
    .I2(custom_comparative_adder_1_o3), .I3(1'b0), .O0(custom_comparative_adder_5_o0),
    .O1(custom_comparative_adder_5_o1), .O2(custom_comparative_adder_5_o2), .O3(Hundreds[1]));
  custom_COMPARATIVE_ADDER custom_comparative_adder_6 (
    .I0(in_1[1]), .I1(custom_comparative_adder_4_o0), .I2(custom_comparative_adder_4_o1),
    .I3(custom_comparative_adder_4_o2), .O0(Units[1]), .O1(Units[2]), .O2(Units[3]), .O3(Tens[0]));
  custom_COMPARATIVE_ADDER custom_comparative_adder_7 (
    .I0(custom_comparative_adder_4_o3), .I1(custom_comparative_adder_5_o0),
    .I2(custom_comparative_adder_5_o1), .I3(custom_comparative_adder_5_o2), .O0(Tens[1]), .O1(Tens[2]),
    .O2(Tens[3]), .O3(Hundreds[0]));
  Hex_Digit_Display hex_digit_display_1 (.value({2'b00, Hundreds[1:0]}));  // open: dp
  Hex_Digit_Display hex_digit_display_2 (.value(Tens));  // open: dp
  Hex_Digit_Display hex_digit_display_3 (.value({Units[3:1], in_1[0]}));  // open: dp

  assign Hundreds[3:2] = 2'b00;
  assign Units[0] = in_1[0];
endmodule

// ADD
module custom_FULL_ADDER (
  input  A,
  input  B,
  input  Carry_IN,
  output Carry_Out,
  output Sum
);

  wire e2_and_1_out_3, e2_and_2_out_3, e6_xor_1_out_3;

  e6_XOR e6_xor_1 (.A(A), .B(B), .out_3(e6_xor_1_out_3));
  e2_AND e2_and_1 (.A(e6_xor_1_out_3), .B(Carry_IN), .out_3(e2_and_1_out_3));
  e2_AND e2_and_2 (.A(A), .B(B), .out_3(e2_and_2_out_3));
  e6_XOR e6_xor_2 (.A(e6_xor_1_out_3), .B(Carry_IN), .out_3(Sum));
  e3_OR e3_or_1 (.A(e2_and_1_out_3), .B(e2_and_2_out_3), .out_3(Carry_Out));
endmodule

// 4BIT_ADDER
module custom_4BIT_ADDER (
  input  I0,
  input  I1,
  input  I2,
  input  I3,
  output S0,
  output S1,
  output S2,
  output S3
);

  wire e2_and_1_out_3, e2_and_2_out_3, e2_and_3_out_3, e2_and_4_out_3, e2_and_5_out_3, e3_or_1_out_3,
       e3_or_2_out_3, e6_xor_2_out_3, e6_xor_3_out_3, e6_xor_4_out_3;

  e6_XOR e6_xor_1 (.A(1'b1), .B(I0), .out_3(S0));
  e2_AND e2_and_1 (.A(1'b1), .B(I0), .out_3(e2_and_1_out_3));
  e6_XOR e6_xor_2 (.A(1'b1), .B(I1), .out_3(e6_xor_2_out_3));
  e2_AND e2_and_2 (.A(1'b1), .B(I1), .out_3(e2_and_2_out_3));
  e6_XOR e6_xor_3 (.A(1'b0), .B(I2), .out_3(e6_xor_3_out_3));
  e2_AND e2_and_3 (.A(1'b0), .B(I2), .out_3(e2_and_3_out_3));
  e6_XOR e6_xor_4 (.A(1'b0), .B(I3), .out_3(e6_xor_4_out_3));
  e6_XOR e6_xor_5 (.A(e2_and_1_out_3), .B(e6_xor_2_out_3), .out_3(S1));
  e2_AND e2_and_4 (.A(e2_and_1_out_3), .B(e6_xor_2_out_3), .out_3(e2_and_4_out_3));
  e3_OR e3_or_1 (.A(e2_and_4_out_3), .B(e2_and_2_out_3), .out_3(e3_or_1_out_3));
  e6_XOR e6_xor_6 (.A(e3_or_1_out_3), .B(e6_xor_3_out_3), .out_3(S2));
  e2_AND e2_and_5 (.A(e3_or_1_out_3), .B(e6_xor_3_out_3), .out_3(e2_and_5_out_3));
  e3_OR e3_or_2 (.A(e2_and_5_out_3), .B(e2_and_3_out_3), .out_3(e3_or_2_out_3));
  e6_XOR e6_xor_7 (.A(e3_or_2_out_3), .B(e6_xor_4_out_3), .out_3(S3));
endmodule

// 4BIT_COMP
module custom_4BIT_COMPARATOR (
  input  B3,
  input  B2,
  input  B1,
  input  B0,
  output _4
);

  wire and_1_out, and_2_out, and_3_out, and_4_out, not_1_out, not_2_out, not_3_out, not_4_out, xnor_1_out,
       xnor_2_out, xnor_3_out;

  not not_1 (not_1_out, 1'b0);
  xnor xnor_1 (xnor_1_out, 1'b0, B3);
  not not_2 (not_2_out, 1'b1);
  not not_3 (not_3_out, 1'b0);
  xnor xnor_2 (xnor_2_out, 1'b1, B2);
  xnor xnor_3 (xnor_3_out, 1'b0, B1);
  not not_4 (not_4_out, 1'b0);
  and and_1 (and_1_out, not_1_out, B3);
  and and_2 (and_2_out, xnor_1_out, not_2_out, B2);
  and and_3 (and_3_out, xnor_1_out, xnor_2_out, not_3_out, B1);
  and and_4 (and_4_out, xnor_1_out, xnor_2_out, xnor_3_out, not_4_out, B0);
  or or_1 (_4, and_1_out, and_2_out, and_3_out, and_4_out);
endmodule

// COMP_ADDER
module custom_COMPARATIVE_ADDER (
  input  I0,
  input  I1,
  input  I2,
  input  I3,
  output O0,
  output O1,
  output O2,
  output O3
);

  wire custom_4bit_comparator_1__4;
  wire [3:0] custom_4bit_adder_1_s0;

  custom_4BIT_ADDER custom_4bit_adder_1 (
    .I0(I0), .I1(I1), .I2(I2), .I3(I3), .S0(custom_4bit_adder_1_s0[0]), .S1(custom_4bit_adder_1_s0[1]),
    .S2(custom_4bit_adder_1_s0[2]), .S3(custom_4bit_adder_1_s0[3]));
  custom_4BIT_COMPARATOR custom_4bit_comparator_1 (
    .B3(I3), .B2(I2), .B1(I1), .B0(I0), ._4(custom_4bit_comparator_1__4));
  Multiplexer #(.width(4)) multiplexer_1 (
    .in0({I3, I2, I1, I0}), .in1(custom_4bit_adder_1_s0), .out({O3, O2, O1, O0}),
    .sel(custom_4bit_comparator_1__4));  // open: en
endmodule
